# Fritzing sketch PiSensor (saved by Fritzing 0.9.3b)
breadboards: 1

parts:
  DHT1 = DHT22 Humidity and Temperature Sensor
  R1 = Resistor [tolerance=±5% resistance=10k package=THT]
  Raspberry_Pi_B_rev1 = Raspberry Pi B rev1
  SGP30_-_Gas = Adafruit SGP30 Gas Sensor [part_number=1782]
  TSL2561_-_Lux = Adafruit TSL2561 [part_number="Adafruit #439"]
  MCP9808_-_Temp = MCP9808 High Accuracy I2C Temperature Sensor [part_number=1782]
  BMP388_-_Pressure = Adafruit_BMP280

nets:
  VIN: DHT1.VDD, R1.Pin_0, Raspberry_Pi_B_rev1.3V3, SGP30_-_Gas.VIN, TSL2561_-_Lux.VIN, MCP9808_-_Temp.VDD, BMP388_-_Pressure.VIN
  N1: DHT1.DATA, R1.Pin_1, Raspberry_Pi_B_rev1.GPIO_4
  GND: DHT1.GND, Raspberry_Pi_B_rev1.GND, SGP30_-_Gas.GND, TSL2561_-_Lux.GND, MCP9808_-_Temp.GND, BMP388_-_Pressure.GND
  N2: Raspberry_Pi_B_rev1.GPIO_0, SGP30_-_Gas.SDA, TSL2561_-_Lux.SDA, MCP9808_-_Temp.SDA, BMP388_-_Pressure.SDI/SDA
  N3: Raspberry_Pi_B_rev1.GPIO_1, SGP30_-_Gas.SCL, TSL2561_-_Lux.SCL, MCP9808_-_Temp.SCL, BMP388_-_Pressure.SCK/SCL

custom parts:
  Adafruit TSL2561: The TSL2561 luminosity sensor is an advanced digital light sensor, ideal for use in a wide range of light situations. Compared to low cost CdS cells, this sensor is more precise, allowing for exact lux calculations and can be configured for different gain/timing ranges to detect light ranges from up to 0.1 - 40,000+ Lux on the fly. The best part of this sensor is that it contains both infrared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
  MCP9808 High Accuracy I2C Temperature Sensor: This I2C digital temperature sensor is one of the more accurate/precise we've ever seen, with a typical accuracy of ±0.25°C over the sensor's -40°C to +125°C range and precision of +0.0625°C. They work great with any microcontroller using standard i2c. There are 3 address pins so you can connect up to 8 to a single I2C bus without address collisions. Best of all, a wide voltage range makes is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
  Adafruit_BMP280: Bosch has stepped up their game with their new BMP280 sensor, an environmental sensor with temperature, barometric pressure that is the next generation upgrade to the BMP085/BMP180/BMP183. This sensor is great for all sorts of weather sensing and can even be used in both I2C and SPI! This precision sensor from Bosch is the best low-cost, precision sensing solution for measuring barometric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
